// Logisim project 00_nor_gate.circ as structural Verilog: 3 circuits, main circuit main
module main (
  input  in_1,
  input  in_2,
  output out_3
);

  NNOR nnor_1 (.O(out_3), .A(in_1), .B(in_2));
endmodule

module PNOR (
  input  A,
  input  B,
  output O
);

  Pull_Resistor #(.pull(1)) pull_resistor_1 (.node(O));
  Transistor #(.\type ("n")) transistor_1 (.in(1'b0), .out(O), .gate(A));
  Transistor #(.\type ("n")) transistor_2 (.in(1'b0), .out(O), .gate(B));
endmodule

module NNOR (
  input  A,
  input  B,
  output O
);

  wire transistor_1_out;

  Transistor transistor_1 (.in(1'b1), .out(transistor_1_out), .gate(A));
  Transistor transistor_2 (.in(transistor_1_out), .out(O), .gate(B));
  Pull_Resistor pull_resistor_1 (.node(O));
endmodule
