// Logisim project main.circ as structural Verilog: 9 circuits, main circuit main
module main (
);

  Multiplexer #(.enable("false")) multiplexer_1 ();  // open: in0, in1, out, sel
endmodule

module Full_Adder (
  input  A,
  input  B,
  input  CI,
  output S,
  output CO
);

  wire and_1_out, and_2_out, or_1_out, xor_1_out;

  xor xor_1 (xor_1_out, A, B);
  and and_1 (and_1_out, CI, or_1_out);
  or or_1 (or_1_out, A, B);
  and and_2 (and_2_out, A, B);
  xor xor_2 (S, xor_1_out, CI);
  or or_2 (CO, and_1_out, and_2_out);
endmodule

module _4_Bit_Ripple_Carry_Adder (
  input  [3:0] A,
  input  CI,
  input  [3:0] B,
  output CO,
  output [3:0] O
);

  wire full_adder_2_co, full_adder_3_co, full_adder_4_co;

  Full_Adder full_adder_1 (.S(O[3]), .CO(CO), .B(B[3]), .CI(full_adder_2_co), .A(A[3]));
  Full_Adder full_adder_2 (.S(O[2]), .CO(full_adder_2_co), .B(B[2]), .CI(full_adder_3_co), .A(A[2]));
  Full_Adder full_adder_3 (.S(O[1]), .CO(full_adder_3_co), .B(B[1]), .CI(full_adder_4_co), .A(A[1]));
  Full_Adder full_adder_4 (.S(O[0]), .CO(full_adder_4_co), .B(B[0]), .CI(CI), .A(A[0]));
endmodule

module _4_Bit_Carry_Lookahead_Logic (
  input  CI,
  input  [3:0] G,
  input  [3:0] P,
  output [3:0] CO,
  output PG,
  output GG
);

  wire and_1_out, and_2_out, and_3_out, and_4_out, and_5_out, and_6_out, and_7_out, and_8_out, and_9_out,
       and_10_out, and_12_out, and_13_out, and_14_out;

  and and_1 (and_1_out, P[0], CI);
  or or_1 (CO[0], and_1_out, G[0]);
  and and_2 (and_2_out, P[1], P[0], CI);
  and and_3 (and_3_out, P[1], G[0]);
  or or_2 (CO[1], and_2_out, and_3_out, G[1]);
  and and_4 (and_4_out, P[2], P[1], P[0], CI);
  and and_5 (and_5_out, P[2], P[1], G[0]);
  and and_6 (and_6_out, P[2], G[1]);
  or or_3 (CO[2], and_4_out, and_5_out, and_6_out, G[2]);
  and and_7 (and_7_out, P[3], P[2], P[1], P[0], CI);
  and and_8 (and_8_out, P[3], P[2], G[1]);
  and and_9 (and_9_out, P[3], G[2]);
  and and_10 (and_10_out, P[3], P[2], P[1], G[0]);
  or or_4 (CO[3], and_7_out, and_10_out, and_8_out, and_9_out, G[3]);
  and and_11 (PG, P[3], P[2], P[1], P[0]);
  and and_12 (and_12_out, P[3], P[2], P[1], G[0]);
  and and_13 (and_13_out, P[3], P[2], G[1]);
  and and_14 (and_14_out, P[3], G[2]);
  or or_5 (GG, and_12_out, and_13_out, and_14_out, G[3]);
endmodule

module _4_Bit_Carry_Lookahead_Generator (
  input  [3:0] A,
  input  [3:0] B,
  input  CI,
  output [3:0] P,
  output [3:0] CO,
  output P03,
  output G03
);

  wire [3:0] G0_out;

  and G0 (G0_out[0], B[0], A[0]);
  and G1 (G0_out[1], B[1], A[1]);
  and G2 (G0_out[2], B[2], A[2]);
  and G3 (G0_out[3], B[3], A[3]);
  xor P0 (P[0], B[0], A[0]);
  xor P1 (P[1], B[1], A[1]);
  xor P2 (P[2], B[2], A[2]);
  xor p3 (P[3], B[3], A[3]);
  _4_Bit_Carry_Lookahead_Logic u_4_bit_carry_lookahead_logic_1 (
    .CO(CO), .PG(P03), .GG(G03), .P(P), .CI(CI), .G(G0_out));
endmodule

module _4_Bit_Carry_Lookahead_Adder (
  input  [3:0] A,
  input  [3:0] B,
  input  CI,
  output G03,
  output P03,
  output CO,
  output [3:0] O
);

  wire [2:0] n4_bit_carry_lookahead_generator_1_co;
  wire [3:0] n4_bit_carry_lookahead_generator_1_p;

  _4_Bit_Carry_Lookahead_Generator u_4_bit_carry_lookahead_generator_1 (
    .P(n4_bit_carry_lookahead_generator_1_p), .CO({CO, n4_bit_carry_lookahead_generator_1_co}), .P03(P03),
    .G03(G03), .B(B), .CI(CI), .A(A));
  xor xor_1 (O[3], n4_bit_carry_lookahead_generator_1_p[3], n4_bit_carry_lookahead_generator_1_co[2]);
  xor xor_2 (O[2], n4_bit_carry_lookahead_generator_1_p[2], n4_bit_carry_lookahead_generator_1_co[1]);
  xor xor_3 (O[1], n4_bit_carry_lookahead_generator_1_p[1], n4_bit_carry_lookahead_generator_1_co[0]);
  xor xor_4 (O[0], n4_bit_carry_lookahead_generator_1_p[0], CI);
endmodule

module _16_Bit_Carry_Lookahead_Generator (
  input  [15:0] A,
  input  [15:0] B,
  input  CI,
  output [15:0] CO,
  output [15:0] PO
);

  wire [3:0] n4_bit_carry_lookahead_generator_1_g03, n4_bit_carry_lookahead_generator_1_p03;
  wire [3:3] n4_bit_carry_lookahead_generator_1_co, n4_bit_carry_lookahead_generator_2_co,
       n4_bit_carry_lookahead_generator_3_co, n4_bit_carry_lookahead_generator_4_co;

  _4_Bit_Carry_Lookahead_Generator u_4_bit_carry_lookahead_generator_1 (
    .P(PO[3:0]), .CO({n4_bit_carry_lookahead_generator_1_co[3], CO[2:0]}),
    .P03(n4_bit_carry_lookahead_generator_1_p03[0]), .G03(n4_bit_carry_lookahead_generator_1_g03[0]),
    .B(A[3:0]), .CI(CI), .A(B[3:0]));
  _4_Bit_Carry_Lookahead_Generator u_4_bit_carry_lookahead_generator_2 (
    .P(PO[7:4]), .CO({n4_bit_carry_lookahead_generator_2_co[3], CO[6:4]}),
    .P03(n4_bit_carry_lookahead_generator_1_p03[1]), .G03(n4_bit_carry_lookahead_generator_1_g03[1]),
    .B(A[7:4]), .CI(CO[3]), .A(B[7:4]));
  _4_Bit_Carry_Lookahead_Generator u_4_bit_carry_lookahead_generator_3 (
    .P(PO[11:8]), .CO({n4_bit_carry_lookahead_generator_3_co[3], CO[10:8]}),
    .P03(n4_bit_carry_lookahead_generator_1_p03[2]), .G03(n4_bit_carry_lookahead_generator_1_g03[2]),
    .B(A[11:8]), .CI(CO[7]), .A(B[11:8]));
  _4_Bit_Carry_Lookahead_Generator u_4_bit_carry_lookahead_generator_4 (
    .P(PO[15:12]), .CO({n4_bit_carry_lookahead_generator_4_co[3], CO[14:12]}),
    .P03(n4_bit_carry_lookahead_generator_1_p03[3]), .G03(n4_bit_carry_lookahead_generator_1_g03[3]),
    .B(A[15:12]), .CI(CO[11]), .A(B[15:12]));
  _4_Bit_Carry_Lookahead_Logic u_4_bit_carry_lookahead_logic_1 (
    .CO({CO[15], CO[11], CO[7], CO[3]}), .P(n4_bit_carry_lookahead_generator_1_p03), .CI(CI),
    .G(n4_bit_carry_lookahead_generator_1_g03));  // open: PG, GG

  // Other names for the same wires on the sheet: C4 = CO[3]; C8 = CO[7]; C12 = CO[11]
endmodule

module _16_Bit_Carry_Lookahead_Adder (
  input  [15:0] A,
  input  [15:0] B,
  input  CI,
  output CO,
  output [15:0] O
);

  wire [14:0] n16_bit_carry_lookahead_generator_1_co;
  wire [15:0] n16_bit_carry_lookahead_generator_1_po;

  _16_Bit_Carry_Lookahead_Generator u_16_bit_carry_lookahead_generator_1 (
    .CO({CO, n16_bit_carry_lookahead_generator_1_co}), .PO(n16_bit_carry_lookahead_generator_1_po), .B(B),
    .CI(CI), .A(A));
  xor xor_1 (O[15], n16_bit_carry_lookahead_generator_1_po[15], n16_bit_carry_lookahead_generator_1_co[14]);
  xor xor_2 (O[14], n16_bit_carry_lookahead_generator_1_po[14], n16_bit_carry_lookahead_generator_1_co[13]);
  xor xor_3 (O[13], n16_bit_carry_lookahead_generator_1_po[13], n16_bit_carry_lookahead_generator_1_co[12]);
  xor xor_4 (O[12], n16_bit_carry_lookahead_generator_1_po[12], n16_bit_carry_lookahead_generator_1_co[11]);
  xor xor_5 (O[11], n16_bit_carry_lookahead_generator_1_po[11], n16_bit_carry_lookahead_generator_1_co[10]);
  xor xor_6 (O[10], n16_bit_carry_lookahead_generator_1_po[10], n16_bit_carry_lookahead_generator_1_co[9]);
  xor xor_7 (O[9], n16_bit_carry_lookahead_generator_1_po[9], n16_bit_carry_lookahead_generator_1_co[8]);
  xor xor_8 (O[8], n16_bit_carry_lookahead_generator_1_po[8], n16_bit_carry_lookahead_generator_1_co[7]);
  xor xor_9 (O[7], n16_bit_carry_lookahead_generator_1_po[7], n16_bit_carry_lookahead_generator_1_co[6]);
  xor xor_10 (O[6], n16_bit_carry_lookahead_generator_1_po[6], n16_bit_carry_lookahead_generator_1_co[5]);
  xor xor_11 (O[5], n16_bit_carry_lookahead_generator_1_po[5], n16_bit_carry_lookahead_generator_1_co[4]);
  xor xor_12 (O[4], n16_bit_carry_lookahead_generator_1_po[4], n16_bit_carry_lookahead_generator_1_co[3]);
  xor xor_13 (O[3], n16_bit_carry_lookahead_generator_1_po[3], n16_bit_carry_lookahead_generator_1_co[2]);
  xor xor_14 (O[2], n16_bit_carry_lookahead_generator_1_po[2], n16_bit_carry_lookahead_generator_1_co[1]);
  xor xor_15 (O[1], n16_bit_carry_lookahead_generator_1_po[1], n16_bit_carry_lookahead_generator_1_co[0]);
  xor xor_16 (O[0], n16_bit_carry_lookahead_generator_1_po[0], CI);
endmodule

module _4_Bit_Adder_Tester (
);

  wire CLK, clock_1_out, comparator_1_gt, comparator_1_lt, FAIL, not_1_out, or_1_out, RCLK;
  wire [2:0] counter_1_q, register_1_q;
  wire [4:0] n4_bit_carry_lookahead_adder_1_o;
  wire [12:0] multiplexer_1_out;

  Clock clock_1 (.out(clock_1_out));
  Counter #(.max('h7), .width(3)) counter_1 (.Q(counter_1_q), .clk(CLK), .clr(FAIL));  // open: load, D, count, carry
  T_Flip_Flop t_ff_1 (.clk(clock_1_out), .T(not_1_out), .Q(CLK), .Qn(RCLK));  // open: preset, reset
  not not_1 (not_1_out, FAIL);
  // Probe on multiplexer_1_out[8:5]
  // Probe on multiplexer_1_out[12:9]
  Multiplexer #(.enable("false"), .select(3), .width(13)) multiplexer_1 (
    .in0(13'h21), .in1(13'h1e30), .in2(13'h1ffe), .in3(13'h142b), .in4(13'h8ca), .in7(13'h8d0),
    .out(multiplexer_1_out), .sel(register_1_q));  // open: in5, in6
  Register #(.width(3)) register_1 (.D(counter_1_q), .Q(register_1_q), .clk(CLK));  // open: en, clr
  _4_Bit_Carry_Lookahead_Adder u_4_bit_carry_lookahead_adder_1 (
    .CO(n4_bit_carry_lookahead_adder_1_o[4]), .O(n4_bit_carry_lookahead_adder_1_o[3:0]),
    .B(multiplexer_1_out[12:9]), .A(multiplexer_1_out[8:5]));  // open: G03, P03, CI
  // Probe on multiplexer_1_out[4:0]
  // Probe on n4_bit_carry_lookahead_adder_1_o
  Comparator #(.width(5)) comparator_1 (
    .a(multiplexer_1_out[4:0]), .b(n4_bit_carry_lookahead_adder_1_o), .gt(comparator_1_gt),
    .lt(comparator_1_lt));  // open: eq
  T_Flip_Flop t_ff_2 (.clk(RCLK), .T(or_1_out), .Q(FAIL));  // open: Qn, preset, reset
  or or_1 (or_1_out, comparator_1_gt, comparator_1_lt);
  LED led_1 (.in(FAIL));
endmodule
