// Logisim project 01_logic_gate.circ as structural Verilog: 1 circuit, main circuit main
module main (
  input  A,
  input  B,
  input  A_2,
  input  A_3,
  input  B_2,
  input  A_4,
  input  B_3,
  input  A_5,
  input  B_4,
  input  A_6,
  input  B_5,
  input  A_7,
  input  A_8,
  input  B_6,
  input  A_9,
  input  B_7,
  input  A_10,
  input  B_8,
  output NAND_O,
  output NOT_O,
  output AND_O,
  output OR_O,
  output XOR_O,
  output NOR_O,
  output NOT_O_2,
  output OR_O_2,
  output AND_O_2,
  output XOR_O_2
);

  wire nand_3_out, nand_4_out, nand_5_out, nand_6_out, nand_7_out, nand_8_out, nor_3_out, nor_4_out,
       nor_5_out, nor_6_out, nor_7_out, nor_8_out, nor_11_out;

  nand nand_1 (NAND_O, A, B);
  nand nand_2 (NOT_O, A_2, A_2);
  nand nand_3 (nand_3_out, A_3, B_2);
  nand nand_4 (nand_4_out, A_4, A_4);
  nand nand_5 (nand_5_out, B_3, B_3);
  nand nand_6 (nand_6_out, A_5, nand_7_out);
  nand nand_7 (nand_7_out, A_5, B_4);
  nand nand_8 (nand_8_out, nand_7_out, B_4);
  nor nor_1 (NOR_O, A_6, B_5);
  nor nor_2 (NOT_O_2, A_7, A_7);
  nor nor_3 (nor_3_out, A_8, B_6);
  nor nor_4 (nor_4_out, A_9, A_9);
  nor nor_5 (nor_5_out, B_7, B_7);
  nor nor_6 (nor_6_out, A_10, A_10);
  nor nor_7 (nor_7_out, B_8, B_8);
  nor nor_8 (nor_8_out, B_8, A_10);
  nand nand_9 (AND_O, nand_3_out, nand_3_out);
  nand nand_10 (OR_O, nand_4_out, nand_5_out);
  nand nand_11 (XOR_O, nand_6_out, nand_8_out);
  nor nor_9 (OR_O_2, nor_3_out, nor_3_out);
  nor nor_10 (AND_O_2, nor_4_out, nor_5_out);
  nor nor_11 (nor_11_out, nor_6_out, nor_7_out);
  nor nor_12 (XOR_O_2, nor_11_out, nor_8_out);

  // Notes on the sheet:
  //   NAND
  //   NAND
  //   NAND
  //   NAND
  //   NOT
  //   AND
  //   AND
  //   OR
  //   XOR
  //   NOR
  //   NOT
  //   OR
  //   AND
  //   XOR
endmodule
